# Fritzing sketch Commander_SwitchOff_Atmega328_SIM800L (saved by Fritzing 0.9.3b)
circuit board: 14.2cm x 11.5cm
breadboards: 1

parts:
  L293D = L293D [package=THT]
  Sensor_IC = atmega328 [package=dip]
  P = screw terminal, 2 pins
  SLOW_FAST = screw terminal, 2 pins
  D1 = Resistor [tolerance=±5% resistance=4.7k part_number=D-5819-3A package=THT]
  R8 = Resistor [tolerance=±5% resistance=3.3k package=THT]
  R12 = Resistor [tolerance=±5% resistance=10k package=THT]
  T+ = screw terminal, 3 pins
  R6 = Resistor [tolerance=±5% resistance=4.7k package=THT]
  R7 = Resistor [tolerance=±5% resistance=10k package=THT]
  XTAL = Crystal [frequency="16 Mhz" package=THT]
  7805 = Voltage Regulator [package=to-220-alt]
  R3 = Resistor [tolerance=±5% resistance=10k package=THT]
  R4 = Resistor [tolerance=±5% resistance=3.3k package=THT]
  R5 = Resistor [tolerance=±5% resistance=10k package=THT]
  R2 = Resistor [tolerance=±5% resistance=400 package=THT]
  R15 = Resistor [tolerance=±5% resistance=1k package=THT]
  C5 = Ceramic Capacitor [capacitance=22pF package="100 mil [THT, multilayer]"]
  C6 = Ceramic Capacitor [capacitance=22pF package="100 mil [THT, multilayer]"]
  C3 = Ceramic Capacitor [capacitance="100 nF" package="100 mil [THT, multilayer]"]
  Q5 = NPN-Transistor [part_number=2N2222A package="TO92 [THT]"]
  Q1 = NPN-Transistor [part_number=2N2222A package="TO92 [THT]"]
  R11 = Resistor [tolerance=±5% resistance=1k package=THT]
  Q3 = NPN-Transistor [part_number=2N2222A package="TO92 [THT]"]
  C16 = Electrolytic Capacitor [capacitance=33µF voltage=10V package="100 mil [THT, electrolytic]"]
  C10 = Electrolytic Capacitor [capacitance=33µF voltage=10V package="100 mil [THT, electrolytic]"]
  C8 = Electrolytic Capacitor [capacitance=33µF voltage=10V package="100 mil [THT, electrolytic]"]
  C7 = Ceramic Capacitor [capacitance="100 nF" package="100 mil [THT, multilayer]"]
  C15 = Ceramic Capacitor [capacitance="100 nF" package="100 mil [THT, multilayer]"]
  C1 = Resistor [tolerance=±5% resistance=220 part_number=C-0.47uF package=THT]
  R1 = Resistor [tolerance=±5% resistance=1k package=THT]
  C2 = Electrolytic Capacitor [capacitance=1mF voltage=25V package="200 mil [THT, electrolytic]"]
  C4 = Electrolytic Capacitor [capacitance=0.47mF voltage=10V package="200 mil [THT, electrolytic]"]
  LED1 = LED - 5mm [color="Red (633nm)" package="5 mm [THT]"]
  Buzzer = screw terminal, 2 pins
  Pad5 = Pad [width=5 height=1 connect=center]
  S1 = Pushbutton [package="[THT]"]
  J59 = rounded female pin header, 3 pins [form="♀ (female rounded)"]
  J60 = rounded female pin header, 3 pins [form="♀ (female rounded)"]  # not connected
  JP7 = Header 2 [package=jst-2-pth]
  JP6 = Header 3 [package=jst-3-pth]
  JP8 = Header 4 [package=jst-4-pth]  # not connected

nets:
  N1: L293D.Out_1_(_Controlled_by_Enable_1_), SLOW_FAST.pin2
  GND: L293D.0V, Sensor_IC.GND, P.pin2, T+.pin1, 7805.GND, R3.Pin_1, C5.0, C6.1, C3.1, Q5.E, Q1.E, Q3.E, C16.-, C10.-, C8.-, C7.0, C15.0, C1.Pin_1, C2.-, C4.-, LED1.cathode, Pad5.pad, S1.Pin_1, S1.Pin_2, JP7.1, JP6.2
  N2: L293D.Out_2_(_Controlled_by_Enable_1_), SLOW_FAST.pin1
  N3: L293D.+Vmotor, D1.Pin_1, 7805.IN, R5.Pin_0, C1.Pin_0, C2.+
  N4: Sensor_IC.RESET, R7.Pin_0, S1.Pin_3, S1.Pin_4
  N5: Sensor_IC.D0_(RX), J59.pin1
  N6: Sensor_IC.D1_(TX), J59.pin2
  N7: Sensor_IC.D2, J59.pin3
  N8: Sensor_IC.D3_(PWM), Sensor_IC.A0, JP6.3
  N9: Sensor_IC.D4, T+.pin3, R6.Pin_0
  N10: Sensor_IC.VCC, Sensor_IC.AVCC, Sensor_IC.AREF, R12.Pin_0, T+.pin2, R6.Pin_1, R7.Pin_1, 7805.OUT, C3.0, C16.+, C10.+, C8.+, C7.1, C15.1, R1.Pin_0, C4.+, JP6.1
  N11: Sensor_IC.XLAT1, XTAL.pin_0, C6.0
  N12: Sensor_IC.XLAT2, XTAL.pin_1, C5.1
  N13: Sensor_IC.D8, R2.Pin_1
  N14: Sensor_IC.A2, R4.Pin_0, R5.Pin_1
  N15: Sensor_IC.A3, R8.Pin_1, JP7.2
  N16: Sensor_IC.A4, R8.Pin_0
  N17: P.pin1, D1.Pin_0
  N18: R3.Pin_0, R2.Pin_0, Q1.B
  N19: R4.Pin_1, Q1.C
  N20: R15.Pin_0, Q5.B
  N21: Q5.C, Buzzer.pin1
  N22: R11.Pin_0, Q3.B
  N23: R1.Pin_1, LED1.anode

notes:
  N
  12V INPUT
  T-
  TD
  M-
  R-
  R+
  1
  STX
  SRX
  J3
  C
  TEMP SENSOR
  RPM SENSOR
  MOTOR
  Krishna
  J4
  Commander
  -
  +
  DTR
  TX
  RX
